// Digital circuit CIRCUITO B.dig as structural Verilog
module CIRCUITO_B (
  input  A,
  input  B,
  input  C,
  input  D,
  output S
);

  wire and_1_out, nand_1_out, nor_1_out, not_1_out, not_2_out, not_3_out;

  not not_1 (not_1_out, A);
  not not_2 (not_2_out, B);
  not not_3 (not_3_out, D);
  nand nand_1 (nand_1_out, C, D);
  and and_1 (and_1_out, not_2_out, C, not_3_out);
  nor nor_1 (nor_1_out, not_1_out, B, nand_1_out);
  or or_1 (S, nor_1_out, and_1_out);
endmodule
