// Digital circuit CIRCUITO A.dig as structural Verilog
module CIRCUITO_A (
  input  B,
  input  A,
  input  C,
  input  D,
  output X
);

  wire nand_1_out, nand_2_out, not_1_out;

  not not_1 (not_1_out, A);
  nand nand_1 (nand_1_out, not_1_out, B);
  nand nand_2 (nand_2_out, ~B, ~C);  // NAnd
  or or_1 (X, ~nand_1_out, ~nand_2_out, ~D);  // Or
endmodule
