// Digital circuit OBT.dig as structural Verilog
module OBT (
  input  B,
  input  C,
  input  F,
  input  P,
  output Obt
);

  wire and_1_out, and_2_out, and_3_out, and_4_out, and_5_out, and_6_out, not_1_out, not_2_out, not_3_out;

  not not_1 (not_1_out, C);
  not not_2 (not_2_out, F);
  not not_3 (not_3_out, P);
  and and_1 (and_1_out, B, C, not_2_out, not_3_out);
  and and_2 (and_2_out, B, C, not_2_out, P);
  and and_3 (and_3_out, B, not_1_out, F, not_3_out);
  and and_4 (and_4_out, B, not_1_out, F, P);
  and and_5 (and_5_out, B, C, F, not_3_out);
  and and_6 (and_6_out, B, C, F, P);
  or or_1 (Obt, and_1_out, and_2_out, and_3_out, and_4_out, and_5_out, and_6_out);
endmodule
