// Digital circuit Circuito Alarme.dig as structural Verilog
module Circuito_Alarme (
  input  Farol,
  input  Porta,
  input  Chave,
  output Alarme
);

  wire and_1_out, and_2_out, not_1_out, not_2_out;

  not not_1 (not_1_out, Farol);
  not not_2 (not_2_out, Chave);
  and and_1 (and_1_out, not_1_out, Porta, Chave);
  and and_2 (and_2_out, Farol, Porta, not_2_out);
  or or_1 (Alarme, and_1_out, and_2_out);
endmodule
