// Logisim project Circuito.circ as structural Verilog: 5 circuits, main circuit main
module main (
  input  [7:0] InsValor,
  input  in_2,
  input  [1:0] RA,
  input  [1:0] RB,
  output [7:0] VA,
  output [7:0] VB
);

  wire demux1x4_1_s0, demux1x4_1_s1, demux1x4_1_s2, demux1x4_1_s3;
  wire [1:1] undriven;
  wire [7:0] R0_q, R1_q, R2_q, R3_q;

  DEMUX1x4 demux1x4_1 (
    .Seletor({undriven[1], in_2}), .S0(demux1x4_1_s0), .S1(demux1x4_1_s1), .S2(demux1x4_1_s2),
    .S3(demux1x4_1_s3));
  Register R0 (.en(demux1x4_1_s0), .Q(R0_q));  // open: D, clk, clr
  Register R1 (.en(demux1x4_1_s1), .Q(R1_q));  // open: D, clk, clr
  Register R2 (.en(demux1x4_1_s2), .Q(R2_q));  // open: D, clk, clr
  Register R3 (.en(demux1x4_1_s3), .Q(R3_q));  // open: D, clk, clr
  MUX4x1 mux4x1_1 (.Entrada_A(R0_q), .Entrada_B(R1_q), .Entrada_C(R2_q), .Entrada_D(R3_q), .Seletor(RA), .out_6(VA));
  MUX4x1 mux4x1_2 (.Entrada_A(R0_q), .Entrada_B(R1_q), .Entrada_C(R2_q), .Entrada_D(R3_q), .Seletor(RB), .out_6(VB));
  // Pins of 1 and 2 bits meet at {undriven[1], in_2}
endmodule

module MUX2x1 (
  input  [7:0] Entrada_A,
  input  [7:0] Entrada_B,
  input  Seletor,
  output [7:0] Saida_8bit
);

  wire not_1_out;
  wire [7:0] and_1_out, and_9_out;

  and and_1 (and_1_out[0], Entrada_A[0], Seletor);
  and and_2 (and_1_out[1], Entrada_A[1], Seletor);
  and and_3 (and_1_out[2], Entrada_A[2], Seletor);
  and and_4 (and_1_out[3], Entrada_A[3], Seletor);
  and and_5 (and_1_out[4], Entrada_A[4], Seletor);
  and and_6 (and_1_out[5], Entrada_A[5], Seletor);
  and and_7 (and_1_out[6], Entrada_A[6], Seletor);
  and and_8 (and_1_out[7], Entrada_A[7], Seletor);
  not not_1 (not_1_out, Seletor);
  and and_9 (and_9_out[0], Entrada_B[0], not_1_out);
  and and_10 (and_9_out[1], Entrada_B[1], not_1_out);
  and and_11 (and_9_out[2], Entrada_B[2], not_1_out);
  and and_12 (and_9_out[3], Entrada_B[3], not_1_out);
  and and_13 (and_9_out[4], Entrada_B[4], not_1_out);
  and and_14 (and_9_out[5], Entrada_B[5], not_1_out);
  and and_15 (and_9_out[6], Entrada_B[6], not_1_out);
  and and_16 (and_9_out[7], Entrada_B[7], not_1_out);
  assign Saida_8bit = and_9_out | and_1_out;  // OR_Gate or_1, 8 bits wide
endmodule

module MUX4x1 (
  input  [7:0] Entrada_A,
  input  [7:0] Entrada_B,
  input  [7:0] Entrada_C,
  input  [7:0] Entrada_D,
  input  [1:0] Seletor,
  output [7:0] out_6
);

  wire demux1x4_1_s0, demux1x4_1_s1, demux1x4_1_s2, demux1x4_1_s3;
  wire [7:0] and_1_out, and_9_out, and_17_out, and_25_out;

  DEMUX1x4 demux1x4_1 (
    .Seletor(Seletor), .S0(demux1x4_1_s0), .S1(demux1x4_1_s1), .S2(demux1x4_1_s2), .S3(demux1x4_1_s3));
  and and_1 (and_1_out[0], Entrada_A[0], demux1x4_1_s0);
  and and_2 (and_1_out[1], Entrada_A[1], demux1x4_1_s0);
  and and_3 (and_1_out[2], Entrada_A[2], demux1x4_1_s0);
  and and_4 (and_1_out[3], Entrada_A[3], demux1x4_1_s0);
  and and_5 (and_1_out[4], Entrada_A[4], demux1x4_1_s0);
  and and_6 (and_1_out[5], Entrada_A[5], demux1x4_1_s0);
  and and_7 (and_1_out[6], Entrada_A[6], demux1x4_1_s0);
  and and_8 (and_1_out[7], Entrada_A[7], demux1x4_1_s0);
  and and_9 (and_9_out[0], Entrada_B[0], demux1x4_1_s1);
  and and_10 (and_9_out[1], Entrada_B[1], demux1x4_1_s1);
  and and_11 (and_9_out[2], Entrada_B[2], demux1x4_1_s1);
  and and_12 (and_9_out[3], Entrada_B[3], demux1x4_1_s1);
  and and_13 (and_9_out[4], Entrada_B[4], demux1x4_1_s1);
  and and_14 (and_9_out[5], Entrada_B[5], demux1x4_1_s1);
  and and_15 (and_9_out[6], Entrada_B[6], demux1x4_1_s1);
  and and_16 (and_9_out[7], Entrada_B[7], demux1x4_1_s1);
  and and_17 (and_17_out[0], Entrada_C[0], demux1x4_1_s2);
  and and_18 (and_17_out[1], Entrada_C[1], demux1x4_1_s2);
  and and_19 (and_17_out[2], Entrada_C[2], demux1x4_1_s2);
  and and_20 (and_17_out[3], Entrada_C[3], demux1x4_1_s2);
  and and_21 (and_17_out[4], Entrada_C[4], demux1x4_1_s2);
  and and_22 (and_17_out[5], Entrada_C[5], demux1x4_1_s2);
  and and_23 (and_17_out[6], Entrada_C[6], demux1x4_1_s2);
  and and_24 (and_17_out[7], Entrada_C[7], demux1x4_1_s2);
  and and_25 (and_25_out[0], Entrada_D[0], demux1x4_1_s3);
  and and_26 (and_25_out[1], Entrada_D[1], demux1x4_1_s3);
  and and_27 (and_25_out[2], Entrada_D[2], demux1x4_1_s3);
  and and_28 (and_25_out[3], Entrada_D[3], demux1x4_1_s3);
  and and_29 (and_25_out[4], Entrada_D[4], demux1x4_1_s3);
  and and_30 (and_25_out[5], Entrada_D[5], demux1x4_1_s3);
  and and_31 (and_25_out[6], Entrada_D[6], demux1x4_1_s3);
  and and_32 (and_25_out[7], Entrada_D[7], demux1x4_1_s3);
  assign out_6 = and_25_out | and_17_out | and_9_out | and_1_out;  // OR_Gate or_1, 8 bits wide
endmodule

module DEMUX1x4 (
  input  [1:0] Seletor,
  output S0,
  output S1,
  output S2,
  output S3
);

  and S00 (S0, ~Seletor[1], ~Seletor[0]);  // AND_Gate
  and S01 (S1, ~Seletor[1], Seletor[0]);  // AND_Gate
  and S10 (S2, Seletor[1], ~Seletor[0]);  // AND_Gate
  and S11 (S3, Seletor[1], Seletor[0]);
endmodule

module Registradores (
);

  Register R0 ();  // open: D, en, clk, Q, clr
  Register R1 ();  // open: D, en, clk, Q, clr
  Register R2 ();  // open: D, en, clk, Q, clr
  Register R3 ();  // open: D, en, clk, Q, clr
endmodule
