// Logisim project CircuitoWriteEnable.circ as structural Verilog: 11 circuits, main circuit main
module main (
  input  [7:0] InsValor,
  input  [1:0] SelRW,
  input  SelValor,
  input  [1:0] SelRA,
  input  [1:0] SelRB,
  input  Gravar,
  input  Ler,
  input  [2:0] SelOp,
  output [7:0] out_9
);

  wire ula_1_c, ula_1_z;
  wire [7:0] mux2x1_1_saida_8bit, registradores_1_va, registradores_1_vb;

  MUX2x1 mux2x1_1 (.Entrada_A(InsValor), .Entrada_B(out_9), .Seletor(SelValor), .Saida_8bit(mux2x1_1_saida_8bit));
  Registradores registradores_1 (
    .Data(mux2x1_1_saida_8bit), .SelRW(SelRW), .SelRA(SelRA), .SelRB(SelRB), .WriteEnable(Gravar),
    .ReadEnable(Ler), .VA(registradores_1_va), .VB(registradores_1_vb));
  // Probe on registradores_1_va
  // Probe on registradores_1_vb
  ULA ula_1 (.SelOp(SelOp), .A(registradores_1_va), .B(registradores_1_vb), .S(out_9), .Z(ula_1_z), .C(ula_1_c));
  LED led_1 (.in(ula_1_z));
  LED led_2 (.in(ula_1_c));
  LedBar ledbar_1 (
    .led0(out_9[7]), .led1(out_9[6]), .led2(out_9[5]), .led3(out_9[4]), .led4(out_9[3]), .led5(out_9[2]),
    .led6(out_9[1]), .led7(out_9[0]));

  // Notes on the sheet:
  //   ax²+bx+c
  //   R0 a = 2
  //   R1 b = 3
  //   R2 c = -4
  //   R3 x = 2
  //   2*2²+3*2+(-4) = 10
  //   000 = A OR B
  //   001 = A*B
  //   010 = A/B
  //   011 = A NOR B
  //   100 = A AND B
  //   101 = ~A
  //   110 = A-B
  //   111 = A+B
endmodule

module MUX2x1 (
  input  [7:0] Entrada_A,
  input  [7:0] Entrada_B,
  input  Seletor,
  output [7:0] Saida_8bit
);

  wire not_1_out;
  wire [7:0] and_1_out, and_9_out;

  not not_1 (not_1_out, Seletor);
  and and_1 (and_1_out[0], Entrada_A[0], not_1_out);
  and and_2 (and_1_out[1], Entrada_A[1], not_1_out);
  and and_3 (and_1_out[2], Entrada_A[2], not_1_out);
  and and_4 (and_1_out[3], Entrada_A[3], not_1_out);
  and and_5 (and_1_out[4], Entrada_A[4], not_1_out);
  and and_6 (and_1_out[5], Entrada_A[5], not_1_out);
  and and_7 (and_1_out[6], Entrada_A[6], not_1_out);
  and and_8 (and_1_out[7], Entrada_A[7], not_1_out);
  and and_9 (and_9_out[0], Entrada_B[0], Seletor);
  and and_10 (and_9_out[1], Entrada_B[1], Seletor);
  and and_11 (and_9_out[2], Entrada_B[2], Seletor);
  and and_12 (and_9_out[3], Entrada_B[3], Seletor);
  and and_13 (and_9_out[4], Entrada_B[4], Seletor);
  and and_14 (and_9_out[5], Entrada_B[5], Seletor);
  and and_15 (and_9_out[6], Entrada_B[6], Seletor);
  and and_16 (and_9_out[7], Entrada_B[7], Seletor);
  assign Saida_8bit = and_9_out | and_1_out;  // OR_Gate or_1, 8 bits wide
endmodule

module MUX4x1 (
  input  [7:0] Entrada_A,
  input  [7:0] Entrada_B,
  input  [7:0] Entrada_C,
  input  [7:0] Entrada_D,
  input  [1:0] Seletor,
  output [7:0] out_6
);

  wire demux1x4_1_s0, demux1x4_1_s1, demux1x4_1_s2, demux1x4_1_s3;
  wire [7:0] and_1_out, and_9_out, and_17_out, and_25_out;

  DEMUX1x4 demux1x4_1 (
    .Seletor(Seletor), .S0(demux1x4_1_s0), .S1(demux1x4_1_s1), .S2(demux1x4_1_s2), .S3(demux1x4_1_s3));
  and and_1 (and_1_out[0], Entrada_A[0], demux1x4_1_s0);
  and and_2 (and_1_out[1], Entrada_A[1], demux1x4_1_s0);
  and and_3 (and_1_out[2], Entrada_A[2], demux1x4_1_s0);
  and and_4 (and_1_out[3], Entrada_A[3], demux1x4_1_s0);
  and and_5 (and_1_out[4], Entrada_A[4], demux1x4_1_s0);
  and and_6 (and_1_out[5], Entrada_A[5], demux1x4_1_s0);
  and and_7 (and_1_out[6], Entrada_A[6], demux1x4_1_s0);
  and and_8 (and_1_out[7], Entrada_A[7], demux1x4_1_s0);
  and and_9 (and_9_out[0], Entrada_B[0], demux1x4_1_s1);
  and and_10 (and_9_out[1], Entrada_B[1], demux1x4_1_s1);
  and and_11 (and_9_out[2], Entrada_B[2], demux1x4_1_s1);
  and and_12 (and_9_out[3], Entrada_B[3], demux1x4_1_s1);
  and and_13 (and_9_out[4], Entrada_B[4], demux1x4_1_s1);
  and and_14 (and_9_out[5], Entrada_B[5], demux1x4_1_s1);
  and and_15 (and_9_out[6], Entrada_B[6], demux1x4_1_s1);
  and and_16 (and_9_out[7], Entrada_B[7], demux1x4_1_s1);
  and and_17 (and_17_out[0], Entrada_C[0], demux1x4_1_s2);
  and and_18 (and_17_out[1], Entrada_C[1], demux1x4_1_s2);
  and and_19 (and_17_out[2], Entrada_C[2], demux1x4_1_s2);
  and and_20 (and_17_out[3], Entrada_C[3], demux1x4_1_s2);
  and and_21 (and_17_out[4], Entrada_C[4], demux1x4_1_s2);
  and and_22 (and_17_out[5], Entrada_C[5], demux1x4_1_s2);
  and and_23 (and_17_out[6], Entrada_C[6], demux1x4_1_s2);
  and and_24 (and_17_out[7], Entrada_C[7], demux1x4_1_s2);
  and and_25 (and_25_out[0], Entrada_D[0], demux1x4_1_s3);
  and and_26 (and_25_out[1], Entrada_D[1], demux1x4_1_s3);
  and and_27 (and_25_out[2], Entrada_D[2], demux1x4_1_s3);
  and and_28 (and_25_out[3], Entrada_D[3], demux1x4_1_s3);
  and and_29 (and_25_out[4], Entrada_D[4], demux1x4_1_s3);
  and and_30 (and_25_out[5], Entrada_D[5], demux1x4_1_s3);
  and and_31 (and_25_out[6], Entrada_D[6], demux1x4_1_s3);
  and and_32 (and_25_out[7], Entrada_D[7], demux1x4_1_s3);
  assign out_6 = and_25_out | and_17_out | and_9_out | and_1_out;  // OR_Gate or_1, 8 bits wide
endmodule

module DEMUX1x4 (
  input  [1:0] Seletor,
  output S0,
  output S1,
  output S2,
  output S3
);

  and S00 (S0, ~Seletor[1], ~Seletor[0]);  // AND_Gate
  and S01 (S1, ~Seletor[1], Seletor[0]);  // AND_Gate
  and S10 (S2, Seletor[1], ~Seletor[0]);  // AND_Gate
  and S11 (S3, Seletor[1], Seletor[0]);
endmodule

module Registradores (
  input  [7:0] Data,
  input  [1:0] SelRW,
  input  [1:0] SelRA,
  input  [1:0] SelRB,
  input  WriteEnable,
  input  ReadEnable,
  output [7:0] VA,
  output [7:0] VB
);

  wire and_1_out, and_2_out, and_3_out, and_4_out, demux1x4_1_s0, demux1x4_1_s1, demux1x4_1_s2,
       demux1x4_1_s3, demux1x4_2_s0, demux1x4_2_s1, demux1x4_2_s2, demux1x4_2_s3, demux1x4_3_s0,
       demux1x4_3_s1, demux1x4_3_s2, demux1x4_3_s3;
  wire [7:0] and_13_out, and_14_out, and_15_out, and_16_out, and_17_out, and_18_out, and_19_out, and_20_out,
       rx_1_q, rx_2_q, rx_3_q, rx_4_q;
  wire [7:7] and_5_out, and_6_out, and_7_out, and_8_out, and_9_out, and_10_out, and_11_out, and_12_out;

  and and_1 (and_1_out, demux1x4_1_s0, WriteEnable);
  and and_2 (and_2_out, demux1x4_1_s1, WriteEnable);
  and and_3 (and_3_out, demux1x4_1_s2, WriteEnable);
  and and_4 (and_4_out, demux1x4_1_s3, WriteEnable);
  DEMUX1x4 demux1x4_1 (.Seletor(SelRW), .S0(demux1x4_1_s0), .S1(demux1x4_1_s1), .S2(demux1x4_1_s2), .S3(demux1x4_1_s3));
  DEMUX1x4 demux1x4_2 (.Seletor(SelRA), .S0(demux1x4_2_s0), .S1(demux1x4_2_s1), .S2(demux1x4_2_s2), .S3(demux1x4_2_s3));
  and and_5 (and_5_out[7], demux1x4_2_s0, ReadEnable);
  and and_6 (and_6_out[7], demux1x4_2_s1, ReadEnable);
  and and_7 (and_7_out[7], demux1x4_2_s2, ReadEnable);
  and and_8 (and_8_out[7], demux1x4_2_s3, ReadEnable);
  RX rx_1 (.Data(Data), .ReadEnable(and_1_out), .Q(rx_1_q));  // open: WriteEnable
  RX rx_2 (.Data(Data), .ReadEnable(and_2_out), .Q(rx_2_q));  // open: WriteEnable
  RX rx_3 (.Data(Data), .ReadEnable(and_3_out), .Q(rx_3_q));  // open: WriteEnable
  RX rx_4 (.Data(Data), .ReadEnable(and_4_out), .Q(rx_4_q));  // open: WriteEnable
  DEMUX1x4 demux1x4_3 (.Seletor(SelRB), .S0(demux1x4_3_s0), .S1(demux1x4_3_s1), .S2(demux1x4_3_s2), .S3(demux1x4_3_s3));
  and and_9 (and_9_out[7], demux1x4_3_s0, ReadEnable);
  and and_10 (and_10_out[7], demux1x4_3_s1, ReadEnable);
  and and_11 (and_11_out[7], demux1x4_3_s2, ReadEnable);
  and and_12 (and_12_out[7], demux1x4_3_s3, ReadEnable);
  assign and_13_out = rx_1_q & {8{and_5_out[7]}};  // AND_Gate and_13, 8 bits wide
  assign and_14_out = rx_2_q & {8{and_6_out[7]}};  // AND_Gate and_14, 8 bits wide
  assign and_15_out = rx_1_q & {8{and_9_out[7]}};  // AND_Gate and_15, 8 bits wide
  assign and_16_out = rx_2_q & {8{and_10_out[7]}};  // AND_Gate and_16, 8 bits wide
  assign and_17_out = rx_3_q & {8{and_7_out[7]}};  // AND_Gate and_17, 8 bits wide
  assign and_18_out = rx_3_q & {8{and_11_out[7]}};  // AND_Gate and_18, 8 bits wide
  assign and_19_out = rx_4_q & {8{and_8_out[7]}};  // AND_Gate and_19, 8 bits wide
  assign and_20_out = rx_4_q & {8{and_12_out[7]}};  // AND_Gate and_20, 8 bits wide
  assign VA = and_13_out | and_14_out | and_17_out | and_19_out;  // OR_Gate or_1, 8 bits wide
  assign VB = and_15_out | and_16_out | and_18_out | and_20_out;  // OR_Gate or_2, 8 bits wide
endmodule

module ULA (
  input  [2:0] SelOp,
  input  [7:0] A,
  input  [7:0] B,
  output [7:0] S,
  output Z,
  output C
);

  wire and_10_out, and_11_out, somador_1_cout, subtrator_1_cout;
  wire [7:0] and_1_out, and_2_out, and_3_out, and_4_out, and_5_out, and_6_out, and_7_out, and_8_out,
       and_9_out, divider_1_out, multiplier_1_out, nor_1_out, not_1_out, not_2_out, or_1_out,
       somador_1_result, subtrator_1_result;
  wire [7:7] demux1x8_1_s0, demux1x8_1_s1, demux1x8_1_s2, demux1x8_1_s3, demux1x8_1_s4, demux1x8_1_s5,
       demux1x8_1_s6, demux1x8_1_s7;

  DEMUX1x8 demux1x8_1 (
    .Seletor(SelOp), .S0(demux1x8_1_s0[7]), .S1(demux1x8_1_s1[7]), .S2(demux1x8_1_s2[7]),
    .S3(demux1x8_1_s3[7]), .S4(demux1x8_1_s4[7]), .S5(demux1x8_1_s5[7]), .S6(demux1x8_1_s6[7]),
    .S7(demux1x8_1_s7[7]));
  Multiplier multiplier_1 (.a(A), .b(B), .out(multiplier_1_out));  // open: cin, cout
  Divider divider_1 (.a(A), .b(B), .out(divider_1_out));  // open: upper, rem
  assign not_1_out = ~A;  // NOT_Gate not_1, 8 bits wide
  assign or_1_out = A | B;  // OR_Gate or_1, 8 bits wide
  assign nor_1_out = ~(A | B);  // NOR_Gate nor_1, 8 bits wide
  assign and_1_out = A & B;  // AND_Gate and_1, 8 bits wide
  Subtrator subtrator_1 (.A(A), .B(B), .Result(subtrator_1_result), .Cout(subtrator_1_cout));
  Somador somador_1 (.A(A), .B(B), .Result(somador_1_result), .Cout(somador_1_cout));
  assign and_2_out = or_1_out & {8{demux1x8_1_s0[7]}};  // AND_Gate and_2, 8 bits wide
  assign and_3_out = multiplier_1_out & {8{demux1x8_1_s1[7]}};  // AND_Gate and_3, 8 bits wide
  assign and_4_out = divider_1_out & {8{demux1x8_1_s2[7]}};  // AND_Gate and_4, 8 bits wide
  assign and_5_out = nor_1_out & {8{demux1x8_1_s3[7]}};  // AND_Gate and_5, 8 bits wide
  assign and_6_out = and_1_out & {8{demux1x8_1_s4[7]}};  // AND_Gate and_6, 8 bits wide
  assign and_7_out = not_1_out & {8{demux1x8_1_s5[7]}};  // AND_Gate and_7, 8 bits wide
  assign and_8_out = subtrator_1_result & {8{demux1x8_1_s6[7]}};  // AND_Gate and_8, 8 bits wide
  assign and_9_out = somador_1_result & {8{demux1x8_1_s7[7]}};  // AND_Gate and_9, 8 bits wide
  and and_10 (and_10_out, subtrator_1_cout, demux1x8_1_s6[7]);
  and and_11 (and_11_out, somador_1_cout, demux1x8_1_s7[7]);
  or or_2 (C, and_11_out, and_10_out);
  assign S = and_2_out | and_3_out | and_4_out | and_5_out | and_6_out | and_7_out | and_8_out | and_9_out;  // OR_Gate or_3, 8 bits wide
  assign not_2_out = ~S;  // NOT_Gate not_2, 8 bits wide
  and and_12 (Z, not_2_out[0], not_2_out[1], not_2_out[2], not_2_out[3], not_2_out[4], not_2_out[5], not_2_out[6], not_2_out[7]);

  // Notes on the sheet:
  //   000 = A OR B
  //   001 = A*B
  //   010 = A/B
  //   011 = A NOR B
  //   100 = A AND B
  //   101 = ~A
  //   110 = A-B
  //   111 = A+B
endmodule

module Somador (
  input  [7:0] A,
  input  [7:0] B,
  output [7:0] Result,
  output Cout
);

  wire somador1bit_1_cout, somador1bit_2_cout, somador1bit_3_cout, somador1bit_4_cout, somador1bit_5_cout,
       somador1bit_6_cout, somador1bit_7_cout;

  Somador1bit somador1bit_1 (.ax(A[0]), .bx(B[0]), .cin(1'b0), .res(Result[0]), .cout(somador1bit_1_cout));
  Somador1bit somador1bit_2 (
    .ax(A[1]), .bx(B[1]), .cin(somador1bit_1_cout), .res(Result[1]), .cout(somador1bit_2_cout));
  Somador1bit somador1bit_3 (
    .ax(A[2]), .bx(B[2]), .cin(somador1bit_2_cout), .res(Result[2]), .cout(somador1bit_3_cout));
  Somador1bit somador1bit_4 (
    .ax(A[3]), .bx(B[3]), .cin(somador1bit_3_cout), .res(Result[3]), .cout(somador1bit_4_cout));
  Somador1bit somador1bit_5 (
    .ax(A[4]), .bx(B[4]), .cin(somador1bit_4_cout), .res(Result[4]), .cout(somador1bit_5_cout));
  Somador1bit somador1bit_6 (
    .ax(A[5]), .bx(B[5]), .cin(somador1bit_5_cout), .res(Result[5]), .cout(somador1bit_6_cout));
  Somador1bit somador1bit_7 (
    .ax(A[6]), .bx(B[6]), .cin(somador1bit_6_cout), .res(Result[6]), .cout(somador1bit_7_cout));
  Somador1bit somador1bit_8 (.ax(A[7]), .bx(B[7]), .cin(somador1bit_7_cout), .res(Result[7]), .cout(Cout));
endmodule

module Somador1bit (
  input  ax,
  input  bx,
  input  cin,
  output res,
  output cout
);

  wire and_1_out, and_2_out, and_3_out, xor_1_out;

  xor xor_1 (xor_1_out, ax, bx);
  and and_1 (and_1_out, ax, bx);
  and and_2 (and_2_out, ax, cin);
  and and_3 (and_3_out, bx, cin);
  xor xor_2 (res, xor_1_out, cin);
  or or_1 (cout, and_1_out, and_2_out, and_3_out);
endmodule

module Subtrator (
  input  [7:0] A,
  input  [7:0] B,
  output [7:0] Result,
  output Cout
);

  wire not_1_out, not_2_out, not_3_out, not_4_out, not_5_out, not_6_out, not_7_out, not_8_out,
       somador1bit_1_cout, somador1bit_2_cout, somador1bit_3_cout, somador1bit_4_cout, somador1bit_5_cout,
       somador1bit_6_cout, somador1bit_7_cout, somador1bit_8_cout;

  not not_1 (not_1_out, B[7]);
  not not_2 (not_2_out, B[6]);
  not not_3 (not_3_out, B[5]);
  not not_4 (not_4_out, B[4]);
  not not_5 (not_5_out, B[3]);
  not not_6 (not_6_out, B[2]);
  not not_7 (not_7_out, B[1]);
  not not_8 (not_8_out, B[0]);
  Somador1bit somador1bit_1 (.ax(A[0]), .bx(not_8_out), .cin(1'b1), .res(Result[0]), .cout(somador1bit_1_cout));
  Somador1bit somador1bit_2 (
    .ax(A[1]), .bx(not_7_out), .cin(somador1bit_1_cout), .res(Result[1]), .cout(somador1bit_2_cout));
  Somador1bit somador1bit_3 (
    .ax(A[2]), .bx(not_6_out), .cin(somador1bit_2_cout), .res(Result[2]), .cout(somador1bit_3_cout));
  Somador1bit somador1bit_4 (
    .ax(A[3]), .bx(not_5_out), .cin(somador1bit_3_cout), .res(Result[3]), .cout(somador1bit_4_cout));
  Somador1bit somador1bit_5 (
    .ax(A[4]), .bx(not_4_out), .cin(somador1bit_4_cout), .res(Result[4]), .cout(somador1bit_5_cout));
  Somador1bit somador1bit_6 (
    .ax(A[5]), .bx(not_3_out), .cin(somador1bit_5_cout), .res(Result[5]), .cout(somador1bit_6_cout));
  Somador1bit somador1bit_7 (
    .ax(A[6]), .bx(not_2_out), .cin(somador1bit_6_cout), .res(Result[6]), .cout(somador1bit_7_cout));
  Somador1bit somador1bit_8 (
    .ax(A[7]), .bx(not_1_out), .cin(somador1bit_7_cout), .res(Result[7]), .cout(somador1bit_8_cout));
  not not_9 (Cout, somador1bit_8_cout);
endmodule

module DEMUX1x8 (
  input  [2:0] Seletor,
  output S0,
  output S1,
  output S2,
  output S3,
  output S4,
  output S5,
  output S6,
  output S7
);

  and and_1 (S0, ~Seletor[2], ~Seletor[1], ~Seletor[0]);  // AND_Gate
  and and_2 (S1, ~Seletor[2], ~Seletor[1], Seletor[0]);  // AND_Gate
  and and_3 (S2, ~Seletor[2], Seletor[1], ~Seletor[0]);  // AND_Gate
  and and_4 (S3, ~Seletor[2], Seletor[1], Seletor[0]);  // AND_Gate
  and and_5 (S4, Seletor[2], ~Seletor[1], ~Seletor[0]);  // AND_Gate
  and and_6 (S5, Seletor[2], ~Seletor[1], Seletor[0]);  // AND_Gate
  and and_7 (S6, Seletor[2], Seletor[1], ~Seletor[0]);  // AND_Gate
  and and_8 (S7, Seletor[2], Seletor[1], Seletor[0]);
endmodule

module RX (
  input  [7:0] Data,
  input  ReadEnable,
  input  WriteEnable,
  output [7:0] Q
);

  wire [7:0] d_ff_1_q;

  D_Flip_Flop d_ff_1 (.D(Data[0]), .clk(ReadEnable), .Q(d_ff_1_q[0]));  // open: Qn, preset, reset
  D_Flip_Flop d_ff_2 (.D(Data[1]), .clk(ReadEnable), .Q(d_ff_1_q[1]));  // open: Qn, preset, reset
  D_Flip_Flop d_ff_3 (.D(Data[2]), .clk(ReadEnable), .Q(d_ff_1_q[2]));  // open: Qn, preset, reset
  D_Flip_Flop d_ff_4 (.D(Data[3]), .clk(ReadEnable), .Q(d_ff_1_q[3]));  // open: Qn, preset, reset
  D_Flip_Flop d_ff_5 (.D(Data[4]), .clk(ReadEnable), .Q(d_ff_1_q[4]));  // open: Qn, preset, reset
  D_Flip_Flop d_ff_6 (.D(Data[5]), .clk(ReadEnable), .Q(d_ff_1_q[5]));  // open: Qn, preset, reset
  D_Flip_Flop d_ff_7 (.D(Data[6]), .clk(ReadEnable), .Q(d_ff_1_q[6]));  // open: Qn, preset, reset
  D_Flip_Flop d_ff_8 (.D(Data[7]), .clk(ReadEnable), .Q(d_ff_1_q[7]));  // open: Qn, preset, reset
  // Probe on d_ff_1_q
  assign Q = d_ff_1_q & {8{WriteEnable}};  // AND_Gate and_1, 8 bits wide
endmodule
