// Logisim project Circuitos_antes_dos_registradores.circ as structural Verilog: 6 circuits, main circuit main
module main (
  input  [7:0] InsValor,
  input  [1:0] in_2,
  input  [1:0] RA,
  input  [1:0] RB,
  output [7:0] VA,
  output [7:0] out_6,
  output [7:0] VB,
  output [7:0] out_8,
  output [7:0] out_9,
  output [7:0] out_10
);

  wire clock_1_out, demux1x4_1_s0, demux1x4_1_s1, demux1x4_1_s2, demux1x4_1_s3;

  DEMUX1x4 demux1x4_1 (.Seletor(in_2), .S0(demux1x4_1_s0), .S1(demux1x4_1_s1), .S2(demux1x4_1_s2), .S3(demux1x4_1_s3));
  Clock clock_1 (.out(clock_1_out));
  Register R0 (.D(InsValor), .en(demux1x4_1_s0), .clk(clock_1_out), .Q(out_6));  // open: clr
  Register R1 (.D(InsValor), .en(demux1x4_1_s1), .clk(clock_1_out), .Q(out_8));  // open: clr
  Register R2 (.D(InsValor), .en(demux1x4_1_s2), .clk(clock_1_out), .Q(out_9));  // open: clr
  Register R3 (.D(InsValor), .en(demux1x4_1_s3), .clk(clock_1_out), .Q(out_10));  // open: clr
  MUX4x1 mux4x1_1 (
    .Entrada_A(out_6), .Entrada_B(out_8), .Entrada_C(out_9), .Entrada_D(out_10), .Seletor(RA), .out_6(VA));
  MUX4x1 mux4x1_2 (
    .Entrada_A(out_6), .Entrada_B(out_8), .Entrada_C(out_9), .Entrada_D(out_10), .Seletor(RB), .out_6(VB));
endmodule

module MUX2x1 (
  input  [7:0] Entrada_A,
  input  [7:0] Entrada_B,
  input  Seletor,
  output [7:0] Saida_8bit
);

  wire not_1_out;
  wire [7:0] and_1_out, and_9_out;

  and and_1 (and_1_out[0], Entrada_A[0], Seletor);
  and and_2 (and_1_out[1], Entrada_A[1], Seletor);
  and and_3 (and_1_out[2], Entrada_A[2], Seletor);
  and and_4 (and_1_out[3], Entrada_A[3], Seletor);
  and and_5 (and_1_out[4], Entrada_A[4], Seletor);
  and and_6 (and_1_out[5], Entrada_A[5], Seletor);
  and and_7 (and_1_out[6], Entrada_A[6], Seletor);
  and and_8 (and_1_out[7], Entrada_A[7], Seletor);
  not not_1 (not_1_out, Seletor);
  and and_9 (and_9_out[0], Entrada_B[0], not_1_out);
  and and_10 (and_9_out[1], Entrada_B[1], not_1_out);
  and and_11 (and_9_out[2], Entrada_B[2], not_1_out);
  and and_12 (and_9_out[3], Entrada_B[3], not_1_out);
  and and_13 (and_9_out[4], Entrada_B[4], not_1_out);
  and and_14 (and_9_out[5], Entrada_B[5], not_1_out);
  and and_15 (and_9_out[6], Entrada_B[6], not_1_out);
  and and_16 (and_9_out[7], Entrada_B[7], not_1_out);
  assign Saida_8bit = and_9_out | and_1_out;  // OR_Gate or_1, 8 bits wide
endmodule

module MUX4x1 (
  input  [7:0] Entrada_A,
  input  [7:0] Entrada_B,
  input  [7:0] Entrada_C,
  input  [7:0] Entrada_D,
  input  [1:0] Seletor,
  output [7:0] out_6
);

  wire demux1x4_1_s0, demux1x4_1_s1, demux1x4_1_s2, demux1x4_1_s3;
  wire [7:0] and_1_out, and_9_out, and_17_out, and_25_out;

  DEMUX1x4 demux1x4_1 (
    .Seletor(Seletor), .S0(demux1x4_1_s0), .S1(demux1x4_1_s1), .S2(demux1x4_1_s2), .S3(demux1x4_1_s3));
  and and_1 (and_1_out[0], Entrada_A[0], demux1x4_1_s0);
  and and_2 (and_1_out[1], Entrada_A[1], demux1x4_1_s0);
  and and_3 (and_1_out[2], Entrada_A[2], demux1x4_1_s0);
  and and_4 (and_1_out[3], Entrada_A[3], demux1x4_1_s0);
  and and_5 (and_1_out[4], Entrada_A[4], demux1x4_1_s0);
  and and_6 (and_1_out[5], Entrada_A[5], demux1x4_1_s0);
  and and_7 (and_1_out[6], Entrada_A[6], demux1x4_1_s0);
  and and_8 (and_1_out[7], Entrada_A[7], demux1x4_1_s0);
  and and_9 (and_9_out[0], Entrada_B[0], demux1x4_1_s1);
  and and_10 (and_9_out[1], Entrada_B[1], demux1x4_1_s1);
  and and_11 (and_9_out[2], Entrada_B[2], demux1x4_1_s1);
  and and_12 (and_9_out[3], Entrada_B[3], demux1x4_1_s1);
  and and_13 (and_9_out[4], Entrada_B[4], demux1x4_1_s1);
  and and_14 (and_9_out[5], Entrada_B[5], demux1x4_1_s1);
  and and_15 (and_9_out[6], Entrada_B[6], demux1x4_1_s1);
  and and_16 (and_9_out[7], Entrada_B[7], demux1x4_1_s1);
  and and_17 (and_17_out[0], Entrada_C[0], demux1x4_1_s2);
  and and_18 (and_17_out[1], Entrada_C[1], demux1x4_1_s2);
  and and_19 (and_17_out[2], Entrada_C[2], demux1x4_1_s2);
  and and_20 (and_17_out[3], Entrada_C[3], demux1x4_1_s2);
  and and_21 (and_17_out[4], Entrada_C[4], demux1x4_1_s2);
  and and_22 (and_17_out[5], Entrada_C[5], demux1x4_1_s2);
  and and_23 (and_17_out[6], Entrada_C[6], demux1x4_1_s2);
  and and_24 (and_17_out[7], Entrada_C[7], demux1x4_1_s2);
  and and_25 (and_25_out[0], Entrada_D[0], demux1x4_1_s3);
  and and_26 (and_25_out[1], Entrada_D[1], demux1x4_1_s3);
  and and_27 (and_25_out[2], Entrada_D[2], demux1x4_1_s3);
  and and_28 (and_25_out[3], Entrada_D[3], demux1x4_1_s3);
  and and_29 (and_25_out[4], Entrada_D[4], demux1x4_1_s3);
  and and_30 (and_25_out[5], Entrada_D[5], demux1x4_1_s3);
  and and_31 (and_25_out[6], Entrada_D[6], demux1x4_1_s3);
  and and_32 (and_25_out[7], Entrada_D[7], demux1x4_1_s3);
  assign out_6 = and_25_out | and_17_out | and_9_out | and_1_out;  // OR_Gate or_1, 8 bits wide
endmodule

module DEMUX1x4 (
  input  [1:0] Seletor,
  output S0,
  output S1,
  output S2,
  output S3
);

  and S00 (S0, ~Seletor[1], ~Seletor[0]);  // AND_Gate
  and S01 (S1, ~Seletor[1], Seletor[0]);  // AND_Gate
  and S10 (S2, Seletor[1], ~Seletor[0]);  // AND_Gate
  and S11 (S3, Seletor[1], Seletor[0]);
endmodule

module Registradores (
  input  [7:0] Data,
  input  RWtoR0,
  input  RWtoR1,
  input  Escreve,
  input  RWtoR2,
  input  [1:0] SelRA,
  input  RWtoR3,
  input  [1:0] SelRB,
  output [7:0] VA,
  output [7:0] VB
);

  wire [7:0] and_1_out, and_2_out, and_3_out, and_4_out, and_5_out, and_6_out, and_7_out, and_8_out,
       register_1_q, register_2_q, register_3_q, register_4_q;
  wire [7:7] demux1x4_1_s0, demux1x4_1_s1, demux1x4_1_s2, demux1x4_1_s3, demux1x4_2_s0, demux1x4_2_s1,
       demux1x4_2_s2, demux1x4_2_s3;

  Register register_1 (.D(Data), .en(RWtoR0), .clk(Escreve), .Q(register_1_q));  // open: clr
  Register register_2 (.D(Data), .en(RWtoR1), .clk(Escreve), .Q(register_2_q));  // open: clr
  Register register_3 (.D(Data), .en(RWtoR2), .clk(Escreve), .Q(register_3_q));  // open: clr
  Register register_4 (.D(Data), .en(RWtoR3), .clk(Escreve), .Q(register_4_q));  // open: clr
  DEMUX1x4 demux1x4_1 (
    .Seletor(SelRA), .S0(demux1x4_1_s0[7]), .S1(demux1x4_1_s1[7]), .S2(demux1x4_1_s2[7]),
    .S3(demux1x4_1_s3[7]));
  DEMUX1x4 demux1x4_2 (
    .Seletor(SelRB), .S0(demux1x4_2_s0[7]), .S1(demux1x4_2_s1[7]), .S2(demux1x4_2_s2[7]),
    .S3(demux1x4_2_s3[7]));
  assign and_1_out = register_1_q & {8{demux1x4_1_s0[7]}};  // AND_Gate and_1, 8 bits wide
  assign and_2_out = register_2_q & {8{demux1x4_1_s1[7]}};  // AND_Gate and_2, 8 bits wide
  assign and_3_out = register_1_q & {8{demux1x4_2_s0[7]}};  // AND_Gate and_3, 8 bits wide
  assign and_4_out = register_2_q & {8{demux1x4_2_s1[7]}};  // AND_Gate and_4, 8 bits wide
  assign and_5_out = register_3_q & {8{demux1x4_1_s2[7]}};  // AND_Gate and_5, 8 bits wide
  assign and_6_out = register_3_q & {8{demux1x4_2_s2[7]}};  // AND_Gate and_6, 8 bits wide
  assign and_7_out = register_4_q & {8{demux1x4_1_s3[7]}};  // AND_Gate and_7, 8 bits wide
  assign and_8_out = register_4_q & {8{demux1x4_2_s3[7]}};  // AND_Gate and_8, 8 bits wide
  assign VA = and_1_out | and_2_out | and_5_out | and_7_out;  // OR_Gate or_1, 8 bits wide
  assign VB = and_3_out | and_4_out | and_6_out | and_8_out;  // OR_Gate or_2, 8 bits wide
endmodule

module demux1x4ENABLE (
  input  [1:0] Seletor,
  input  Enable,
  output S0,
  output S1,
  output S2,
  output S3
);

  wire S00_out, S01_out, S10_out, S11_out;

  and S00 (S00_out, ~Seletor[1], ~Seletor[0]);  // AND_Gate
  and S01 (S01_out, ~Seletor[1], Seletor[0]);  // AND_Gate
  and S10 (S10_out, Seletor[1], ~Seletor[0]);  // AND_Gate
  and S11 (S11_out, Seletor[1], Seletor[0]);
  and and_1 (S0, S00_out, Enable);
  and and_2 (S1, S01_out, Enable);
  and and_3 (S2, S10_out, Enable);
  and and_4 (S3, S11_out, Enable);
endmodule
