// Digital circuit FPGA.dig as structural Verilog
module FPGA (
);

  wire SW0_out, u_fpga_out;

  LED LEDR8 ();  // open: in
  LED LEDR9 ();  // open: in
  DipSwitch SW9 ();  // open: out
  DipSwitch SW8 ();  // open: out
  LED LEDR6 ();  // open: in
  LED LEDR7 ();  // open: in
  DipSwitch SW7 ();  // open: out
  DipSwitch SW6 ();  // open: out
  LED LEDR4 ();  // open: in
  LED LEDR5 ();  // open: in
  DipSwitch SW5 ();  // open: out
  DipSwitch SW4 ();  // open: out
  LED LEDR2 ();  // open: in
  LED LEDR3 ();  // open: in
  DipSwitch SW3 ();  // open: out
  DipSwitch SW2 ();  // open: out
  LED LEDR0 (.in(u_fpga_out));
  LED LEDR1 ();  // open: in
  DipSwitch SW1 ();  // open: out
  DipSwitch SW0 (.out(SW0_out));
  fpga u_fpga (.in(SW0_out), .out(u_fpga_out));
  LED LEDG7 ();  // open: in
  Button KEY3 ();  // open: out
  LED LEDG5 ();  // open: in
  LED LEDG6 ();  // open: in
  Button KEY2 ();  // open: out
  LED LEDG3 ();  // open: in
  LED LEDG4 ();  // open: in
  Button KEY1 ();  // open: out
  LED LEDG1 ();  // open: in
  LED LEDG2 ();  // open: in
  Button KEY0 ();  // open: out
  LED LEDG0 ();  // open: in
endmodule

/* Code of fpga:
library ieee;
use ieee.std_logic_1164.ALL;

entity fpga is
	port (
		sw: in std_logic_vector (9 downto 0);
		ledr: out std_logic_vector (9 downto 0);
		hex3: out std_logic_vector (6 downto 0);
		hex2: out std_logic_vector (6 downto 0);
		hex1: out std_logic_vector (6 downto 0);
		hex0: out std_logic_vector (6 downto 0)
	);
end entity fpga;

architecture behav_fluxo of fpga is 
	begin
		ledr(0) <= sw(0);
end behav_fluxo;
*/
