// Digital circuit Contador de Gray 4bit.dig as structural Verilog
module Contador_de_Gray_4bit (
  input  CLOCK,
  output B1,
  output B2,
  output B3,
  output B0
);

  wire and_1_out, and_2_out, and_3_out, and_4_out, and_5_out, and_6_out, and_7_out, and_8_out, and_9_out,
       and_10_out, or_1_out, or_2_out, Q0_nq, Q1_nq, Q2_nq, Q3_nq, xnor_1_out, xnor_2_out, xnor_3_out,
       xor_1_out, xor_2_out, xor_3_out;

  xor xor_1 (xor_1_out, B3, B1);
  xnor xnor_1 (xnor_1_out, B3, B1);
  and and_1 (and_1_out, B2, xor_1_out);
  and and_2 (and_2_out, xnor_1_out, Q2_nq);
  xnor xnor_2 (xnor_2_out, B1, B2);
  xor xor_2 (xor_2_out, B1, B2);
  or or_1 (or_1_out, and_1_out, and_2_out);
  and and_3 (and_3_out, xnor_2_out, B3);
  and and_4 (and_4_out, Q3_nq, xor_2_out);
  or or_2 (or_2_out, and_3_out, and_4_out);
  JK_FF Q0 (.J(or_1_out), .C(CLOCK), .K(or_2_out), .Q(B0), .nQ(Q0_nq));
  xnor xnor_3 (xnor_3_out, B3, B2);
  xor xor_3 (xor_3_out, B3, B2);
  and and_5 (and_5_out, B0, xnor_3_out);
  and and_6 (and_6_out, B0, xor_3_out);
  JK_FF Q1 (.J(and_5_out), .C(CLOCK), .K(and_6_out), .Q(B1), .nQ(Q1_nq));
  and and_7 (and_7_out, B1, Q0_nq, Q3_nq);
  and and_8 (and_8_out, B3, B1, Q0_nq);
  JK_FF Q2 (.J(and_7_out), .C(CLOCK), .K(and_8_out), .Q(B2), .nQ(Q2_nq));
  and and_9 (and_9_out, B2, Q0_nq, Q1_nq);
  and and_10 (and_10_out, Q0_nq, Q1_nq, Q2_nq);
  JK_FF Q3 (.J(and_9_out), .C(CLOCK), .K(and_10_out), .Q(B3), .nQ(Q3_nq));
endmodule
