// Digital circuit ContadorGray.dig as structural Verilog
module ContadorGray (
  input  clk
);

  wire and_1_out, and_2_out, and_3_out, and_4_out, and_5_out, and_6_out, and_7_out, and_8_out, and_9_out,
       and_10_out, or_1_out, or_2_out, Q0_nq, Q0_q, Q1_nq, Q1_q, Q2_nq, Q2_q, Q3_nq, Q3_q, xnor_1_out,
       xnor_2_out, xnor_3_out, xor_1_out, xor_2_out, xor_3_out;

  xor xor_1 (xor_1_out, Q2_q, Q1_q);
  and and_1 (and_1_out, xor_1_out, Q3_nq, Q0_q);
  xnor xnor_1 (xnor_1_out, Q2_q, Q1_q);
  and and_2 (and_2_out, xnor_1_out, Q3_q, Q0_q);
  xnor xnor_2 (xnor_2_out, Q3_q, Q1_q);
  and and_3 (and_3_out, xnor_2_out, Q2_nq, Q0_nq);
  xor xor_2 (xor_2_out, Q3_q, Q1_q);
  and and_4 (and_4_out, xor_2_out, Q2_q, Q0_nq);
  or or_1 (or_1_out, and_1_out, and_2_out);
  or or_2 (or_2_out, and_3_out, and_4_out);
  LED led_1 (.in(Q3_q));
  JK_FF Q0 (.J(or_2_out), .C(clk), .K(or_1_out), .Q(Q0_q), .nQ(Q0_nq));
  LED led_2 (.in(Q2_q));
  LED led_3 (.in(Q1_q));
  LED led_4 (.in(Q0_q));
  xnor xnor_3 (xnor_3_out, Q3_q, Q2_q);
  and and_5 (and_5_out, xnor_3_out, Q1_nq, Q0_q);
  xor xor_3 (xor_3_out, Q2_q, Q3_q);
  and and_6 (and_6_out, xor_3_out, Q1_q, Q0_q);
  JK_FF Q1 (.J(and_5_out), .C(clk), .K(and_6_out), .Q(Q1_q), .nQ(Q1_nq));
  and and_7 (and_7_out, Q3_nq, Q2_nq, Q1_q, Q0_nq);
  and and_8 (and_8_out, Q3_q, Q2_q, Q1_q, Q0_nq);
  JK_FF Q2 (.J(and_7_out), .C(clk), .K(and_8_out), .Q(Q2_q), .nQ(Q2_nq));
  and and_9 (and_9_out, Q3_nq, Q2_q, Q1_nq, Q0_nq);
  and and_10 (and_10_out, Q3_q, Q2_nq, Q1_nq, Q0_nq);
  JK_FF Q3 (.J(and_9_out), .C(clk), .K(and_10_out), .Q(Q3_q), .nQ(Q3_nq));
endmodule
