// Digital circuit blackjack.dig as structural Verilog
module blackjack (
);

  External u_external_1 ();  // open: in, out
endmodule

/* Code of External:
LIBRARY ieee;
USE ieee.std_logic_1164.ALL;

ENTITY blackjack IS PORT(
	hit: in STD_LOGIC;
	stay: in STD_LOGIC;
	start: in STD_LOGIC;
	cards: in STD_LOGIC;
*/
