// Logisim project 3bit_adder.circ as structural Verilog: 2 circuits, main circuit main
module main (
  input  [2:0] in_1,
  input  [2:0] in_2,
  output [2:0] out_3,
  output out_4
);

  wire half_adder_2_carry, half_adder_3_carry;

  half_adder half_adder_1 (.a(in_1[2]), .b(in_2[2]), .carry_in(half_adder_2_carry), .sum(out_3[2]), .carry(out_4));
  half_adder half_adder_2 (
    .a(in_1[1]), .b(in_2[1]), .carry_in(half_adder_3_carry), .sum(out_3[1]), .carry(half_adder_2_carry));
  half_adder half_adder_3 (.a(in_1[0]), .b(in_2[0]), .carry_in(1'b0), .sum(out_3[0]), .carry(half_adder_3_carry));
endmodule

module half_adder (
  input  a,
  input  b,
  input  carry_in,
  output sum,
  output carry
);

  wire and_1_out, and_2_out, or_1_out, xor_1_out;

  xor xor_1 (xor_1_out, b, a);
  and and_1 (and_1_out, b, a);
  or or_1 (or_1_out, a, b);
  and and_2 (and_2_out, or_1_out, carry_in);
  xor xor_2 (sum, xor_1_out, carry_in);
  or or_2 (carry, and_1_out, and_2_out);
endmodule
